// Logisim project CPU.circ as structural Verilog: 22 circuits, main circuit RegisterFile2
// RF2
module RegisterFile2 (
  input  rd1,
  input  rd2,
  input  [17:0] \input ,
  input  wd1,
  input  we,
  output [17:0] output1,
  output [17:0] output2
);

  wire not_1_out, not_2_out, not_3_out;
  wire [17:0] R0_q, R1_q;

  Register #(.width(18)) R0 (.D(\input ), .en(not_1_out), .Q(R0_q), .clk(we));  // open: clr
  not not_1 (not_1_out, wd1);
  Register #(.width(18)) R1 (.D(\input ), .en(wd1), .Q(R1_q), .clk(we));  // open: clr
  not not_2 (not_2_out, rd1);
  assign output1 = not_2_out ? R0_q : 18'bz;  // Controlled_Buffer controlled_buffer_1
  not not_3 (not_3_out, rd2);
  assign output2 = not_3_out ? R0_q : 18'bz;  // Controlled_Buffer controlled_buffer_2
  assign output1 = rd1 ? R1_q : 18'bz;  // Controlled_Buffer controlled_buffer_3
  assign output2 = rd2 ? R1_q : 18'bz;  // Controlled_Buffer controlled_buffer_4
endmodule

// RF4
module RegisterFile4 (
  input  [1:0] rd1,
  input  [1:0] rd2,
  input  [17:0] \input ,
  input  [1:0] wd1,
  input  we,
  output [17:0] output1,
  output [17:0] output2
);

  wire not_1_out, not_2_out, pathpicker_1_o0, pathpicker_1_o1;
  wire [17:0] registerfile2_1_output1, registerfile2_1_output2, registerfile2_2_output1,
       registerfile2_2_output2;

  PathPicker pathpicker_1 (.i0(we), .\default (1'b0), .select(wd1[1]), .o0(pathpicker_1_o0), .o1(pathpicker_1_o1));
  RegisterFile2 registerfile2_1 (
    .rd1(rd1[0]), .rd2(rd2[0]), .\input (\input ), .wd1(wd1[0]), .we(pathpicker_1_o0),
    .output1(registerfile2_1_output1), .output2(registerfile2_1_output2));
  RegisterFile2 registerfile2_2 (
    .rd1(rd1[0]), .rd2(rd2[0]), .\input (\input ), .wd1(wd1[0]), .we(pathpicker_1_o1),
    .output1(registerfile2_2_output1), .output2(registerfile2_2_output2));
  not not_1 (not_1_out, rd1[1]);
  assign output1 = not_1_out ? registerfile2_1_output1 : 18'bz;  // Controlled_Buffer controlled_buffer_1
  assign output1 = rd1[1] ? registerfile2_2_output1 : 18'bz;  // Controlled_Buffer controlled_buffer_2
  assign output2 = rd2[1] ? registerfile2_2_output2 : 18'bz;  // Controlled_Buffer controlled_buffer_3
  not not_2 (not_2_out, rd2[1]);
  assign output2 = not_2_out ? registerfile2_1_output2 : 18'bz;  // Controlled_Buffer controlled_buffer_4
endmodule

// RF8
module RegisterFile8 (
  input  [2:0] rd1,
  input  [2:0] rd2,
  input  [17:0] \input ,
  input  [2:0] wd1,
  input  we,
  output [17:0] output1,
  output [17:0] output2
);

  wire not_1_out, not_2_out, pathpicker_1_o0, pathpicker_1_o1;
  wire [17:0] registerfile4_1_output1, registerfile4_1_output2, registerfile4_2_output1,
       registerfile4_2_output2;

  PathPicker pathpicker_1 (.i0(we), .\default (1'b0), .select(wd1[2]), .o0(pathpicker_1_o0), .o1(pathpicker_1_o1));
  RegisterFile4 registerfile4_1 (
    .rd1(rd1[1:0]), .rd2(rd2[1:0]), .\input (\input ), .wd1(wd1[1:0]), .we(pathpicker_1_o0),
    .output1(registerfile4_1_output1), .output2(registerfile4_1_output2));
  RegisterFile4 registerfile4_2 (
    .rd1(rd1[1:0]), .rd2(rd2[1:0]), .\input (\input ), .wd1(wd1[1:0]), .we(pathpicker_1_o1),
    .output1(registerfile4_2_output1), .output2(registerfile4_2_output2));
  not not_1 (not_1_out, rd1[2]);
  assign output1 = not_1_out ? registerfile4_1_output1 : 18'bz;  // Controlled_Buffer controlled_buffer_1
  assign output1 = rd1[2] ? registerfile4_2_output1 : 18'bz;  // Controlled_Buffer controlled_buffer_2
  not not_2 (not_2_out, rd2[2]);
  assign output2 = not_2_out ? registerfile4_1_output2 : 18'bz;  // Controlled_Buffer controlled_buffer_3
  assign output2 = rd2[2] ? registerfile4_2_output2 : 18'bz;  // Controlled_Buffer controlled_buffer_4
endmodule

// RF16
module RegisterFile16 (
  input  [3:0] rd1,
  input  [3:0] rd2,
  input  [17:0] \input ,
  input  [3:0] wd1,
  input  we,
  output [17:0] output1,
  output [17:0] output2
);

  wire not_1_out, not_2_out, pathpicker_1_o0, pathpicker_1_o1;
  wire [17:0] registerfile8_1_output1, registerfile8_1_output2, registerfile8_2_output1,
       registerfile8_2_output2;

  PathPicker pathpicker_1 (.i0(we), .\default (1'b0), .select(wd1[3]), .o0(pathpicker_1_o0), .o1(pathpicker_1_o1));
  RegisterFile8 registerfile8_1 (
    .rd1(rd1[2:0]), .rd2(rd2[2:0]), .\input (\input ), .wd1(wd1[2:0]), .we(pathpicker_1_o0),
    .output1(registerfile8_1_output1), .output2(registerfile8_1_output2));
  RegisterFile8 registerfile8_2 (
    .rd1(rd1[2:0]), .rd2(rd2[2:0]), .\input (\input ), .wd1(wd1[2:0]), .we(pathpicker_1_o1),
    .output1(registerfile8_2_output1), .output2(registerfile8_2_output2));
  not not_1 (not_1_out, rd1[3]);
  assign output1 = not_1_out ? registerfile8_1_output1 : 18'bz;  // Controlled_Buffer controlled_buffer_1
  assign output1 = rd1[3] ? registerfile8_2_output1 : 18'bz;  // Controlled_Buffer controlled_buffer_2
  not not_2 (not_2_out, rd2[3]);
  assign output2 = not_2_out ? registerfile8_1_output2 : 18'bz;  // Controlled_Buffer controlled_buffer_3
  assign output2 = rd2[3] ? registerfile8_2_output2 : 18'bz;  // Controlled_Buffer controlled_buffer_4
endmodule

// PP
module PathPicker (
  input  select,
  input  i0,
  input  \default ,
  output o0,
  output o1
);

  wire not_1_out;

  not not_1 (not_1_out, select);
  assign o1 = select ? i0 : 1'bz;  // Controlled_Buffer controlled_buffer_1
  assign o0 = not_1_out ? i0 : 1'bz;  // Controlled_Buffer controlled_buffer_2
  assign o1 = not_1_out ? \default  : 1'bz;  // Controlled_Buffer controlled_buffer_3
  assign o0 = select ? \default  : 1'bz;  // Controlled_Buffer controlled_buffer_4
endmodule

module ADD1 (
  input  carry_in,
  input  input0,
  input  input1,
  output \output ,
  output carry_out
);

  wire and_1_out, and_2_out, xor_1_out;

  xor xor_1 (xor_1_out, input0, input1);
  and and_1 (and_1_out, input0, input1);
  and and_2 (and_2_out, carry_in, xor_1_out);
  or or_1 (carry_out, and_1_out, and_2_out);
  xor xor_2 (\output , carry_in, xor_1_out);
endmodule

module ADD2 (
  input  carry_in,
  input  [1:0] input0,
  input  [1:0] input1,
  output [1:0] \output ,
  output carry_out
);

  wire add1_1_carry_out;

  ADD1 add1_1 (
    .input0(input0[0]), .input1(input1[0]), .carry_in(carry_in), .carry_out(add1_1_carry_out),
    .\output (\output [0]));
  ADD1 add1_2 (
    .input0(input0[1]), .input1(input1[1]), .carry_in(add1_1_carry_out), .carry_out(carry_out),
    .\output (\output [1]));
endmodule

module ADD4 (
  input  carry_in,
  input  [3:0] input0,
  input  [3:0] input1,
  output [3:0] out_4,
  output carry_out
);

  wire add2_1_carry_out;

  ADD2 add2_1 (
    .input0(input0[1:0]), .input1(input1[1:0]), .carry_in(carry_in), .carry_out(add2_1_carry_out),
    .\output (out_4[1:0]));
  ADD2 add2_2 (
    .input0(input0[3:2]), .input1(input1[3:2]), .carry_in(add2_1_carry_out), .carry_out(carry_out),
    .\output (out_4[3:2]));
endmodule

module ADD8 (
  input  carry_in,
  input  [7:0] input0,
  input  [7:0] input1,
  output [7:0] out_4,
  output carry_out
);

  wire add4_1_carry_out;

  ADD4 add4_1 (
    .input0(input0[3:0]), .input1(input1[3:0]), .carry_in(carry_in), .carry_out(add4_1_carry_out),
    .out_4(out_4[3:0]));
  ADD4 add4_2 (
    .input0(input0[7:4]), .input1(input1[7:4]), .carry_in(add4_1_carry_out), .carry_out(carry_out),
    .out_4(out_4[7:4]));
endmodule

module ADD18 (
  input  [17:0] input0,
  input  [17:0] input1,
  output [17:0] \output ,
  output carry_out
);

  wire add8_1_carry_out, add8_2_carry_out;

  ADD8 add8_1 (
    .input0(input0[7:0]), .input1(input1[7:0]), .carry_in(1'b0), .carry_out(add8_1_carry_out),
    .out_4(\output [7:0]));
  ADD8 add8_2 (
    .input0(input0[15:8]), .input1(input1[15:8]), .carry_in(add8_1_carry_out), .carry_out(add8_2_carry_out),
    .out_4(\output [15:8]));
  ADD2 add2_1 (
    .input0(input0[17:16]), .input1(input1[17:16]), .carry_in(add8_2_carry_out), .carry_out(carry_out),
    .\output (\output [17:16]));
endmodule

// C1
module Comparator1 (
  input  in_lt,
  input  in_eq,
  input  in_gt,
  input  a,
  input  b,
  output out_lt,
  output out_eq,
  output out_gt
);

  wire and_1_out, and_2_out, and_4_out, xnor_1_out;

  xnor xnor_1 (xnor_1_out, a, b);
  and and_1 (and_1_out, in_eq, ~xnor_1_out);  // AND_Gate
  or or_1 (out_lt, in_lt, and_2_out);
  and and_2 (and_2_out, b, and_1_out);
  and and_3 (out_eq, xnor_1_out, in_eq);
  and and_4 (and_4_out, a, and_1_out);
  or or_2 (out_gt, and_4_out, in_gt);
endmodule

// C2
module Comparator2 (
  input  in_lt,
  input  in_eq,
  input  in_gt,
  input  [1:0] a,
  input  [1:0] b,
  output out_lt,
  output out_eq,
  output out_gt
);

  wire comparator1_1_out_eq, comparator1_1_out_gt, comparator1_1_out_lt;

  Comparator1 comparator1_1 (
    .a(a[1]), .b(b[1]), .in_lt(in_lt), .in_eq(in_eq), .in_gt(in_gt), .out_lt(comparator1_1_out_lt),
    .out_eq(comparator1_1_out_eq), .out_gt(comparator1_1_out_gt));
  Comparator1 comparator1_2 (
    .a(a[0]), .b(b[0]), .in_lt(comparator1_1_out_lt), .in_eq(comparator1_1_out_eq),
    .in_gt(comparator1_1_out_gt), .out_lt(out_lt), .out_eq(out_eq), .out_gt(out_gt));
endmodule

// C4
module Comparator4 (
  input  in_lt,
  input  in_eq,
  input  in_gt,
  input  [3:0] a,
  input  [3:0] b,
  output out_lt,
  output out_eq,
  output out_gt
);

  wire comparator2_1_out_eq, comparator2_1_out_gt, comparator2_1_out_lt;

  Comparator2 comparator2_1 (
    .a(a[3:2]), .b(b[3:2]), .in_lt(in_lt), .in_eq(in_eq), .in_gt(in_gt), .out_lt(comparator2_1_out_lt),
    .out_eq(comparator2_1_out_eq), .out_gt(comparator2_1_out_gt));
  Comparator2 comparator2_2 (
    .a(a[1:0]), .b(b[1:0]), .in_lt(comparator2_1_out_lt), .in_eq(comparator2_1_out_eq),
    .in_gt(comparator2_1_out_gt), .out_lt(out_lt), .out_eq(out_eq), .out_gt(out_gt));
endmodule

// C8
module Comparator8 (
  input  in_lt,
  input  in_eq,
  input  in_gt,
  input  [7:0] a,
  input  [7:0] b,
  output out_lt,
  output out_eq,
  output out_gt
);

  wire comparator4_1_out_eq, comparator4_1_out_gt, comparator4_1_out_lt;

  Comparator4 comparator4_1 (
    .a(a[7:4]), .b(b[7:4]), .in_lt(in_lt), .in_eq(in_eq), .in_gt(in_gt), .out_lt(comparator4_1_out_lt),
    .out_eq(comparator4_1_out_eq), .out_gt(comparator4_1_out_gt));
  Comparator4 comparator4_2 (
    .a(a[3:0]), .b(b[3:0]), .in_lt(comparator4_1_out_lt), .in_eq(comparator4_1_out_eq),
    .in_gt(comparator4_1_out_gt), .out_lt(out_lt), .out_eq(out_eq), .out_gt(out_gt));
endmodule

// C18
module Comparator18 (
  input  [17:0] a,
  input  [17:0] b,
  output out_lt,
  output out_eq,
  output out_gt
);

  wire comparator8_1_out_eq, comparator8_1_out_gt, comparator8_1_out_lt, comparator8_2_out_eq,
       comparator8_2_out_gt, comparator8_2_out_lt;

  Comparator8 comparator8_1 (
    .a(a[17:10]), .b(b[17:10]), .in_lt(1'b0), .in_eq(1'b1), .in_gt(1'b0), .out_lt(comparator8_1_out_lt),
    .out_eq(comparator8_1_out_eq), .out_gt(comparator8_1_out_gt));
  Comparator8 comparator8_2 (
    .a(a[9:2]), .b(b[9:2]), .in_lt(comparator8_1_out_lt), .in_eq(comparator8_1_out_eq),
    .in_gt(comparator8_1_out_gt), .out_lt(comparator8_2_out_lt), .out_eq(comparator8_2_out_eq),
    .out_gt(comparator8_2_out_gt));
  Comparator2 comparator2_1 (
    .a(a[1:0]), .b(b[1:0]), .in_lt(comparator8_2_out_lt), .in_eq(comparator8_2_out_eq),
    .in_gt(comparator8_2_out_gt), .out_lt(out_lt), .out_eq(out_eq), .out_gt(out_gt));
endmodule

module Main (
);

  wire clock_1_out, controlunit_1_branch, controlunit_1_imm_select, controlunit_1_pcwe, controlunit_1_s_ram,
       controlunit_1_we, controlunit_1_winput;
  wire [2:0] controlunit_1_alu_op, controlunit_1_nzp;
  wire [3:0] controlunit_1_rd1, controlunit_1_rd2, controlunit_1_wd;
  wire [9:0] controlunit_1_ram_address;
  wire [17:0] alu_1_out, controlunit_1_branch_offset, controlunit_1_imm, multiplexer_1_out,
       multiplexer_2_out, pc_1_output, ram_1_data, registerfile16_1_output1, registerfile16_1_output2,
       rom_1_data;

  Clock clock_1 (.out(clock_1_out));
  PC pc_1 (
    .branch_offset(controlunit_1_branch_offset), .we(controlunit_1_pcwe), .branch(controlunit_1_branch),
    .op1(registerfile16_1_output1), .op2(registerfile16_1_output2), .nzp(controlunit_1_nzp),
    .\output (pc_1_output));
  ROM #(.addrWidth(18), .dataWidth(18)) rom_1 (.addr(pc_1_output), .data(rom_1_data), .sel(1'b1));
  ControlUnit controlunit_1 (
    .inst(rom_1_data), .nzp(controlunit_1_nzp), .branch(controlunit_1_branch), .pcwe(controlunit_1_pcwe),
    .branch_offset(controlunit_1_branch_offset), .ram_address(controlunit_1_ram_address),
    .alu_op(controlunit_1_alu_op), .s_ram(controlunit_1_s_ram), .imm_select(controlunit_1_imm_select),
    .imm(controlunit_1_imm), .winput(controlunit_1_winput), .clock(clock_1_out), .rd1(controlunit_1_rd1),
    .rd2(controlunit_1_rd2), .wd(controlunit_1_wd), .we(controlunit_1_we));
  RAM #(.addrWidth(10), .dataWidth(18), .bus("separate")) ram_1 (
    .addr(controlunit_1_ram_address), .din(registerfile16_1_output1), .data(ram_1_data),
    .str(controlunit_1_s_ram), .sel(1'b1), .clk(clock_1_out));  // open: ld, clr
  Multiplexer #(.width(18), .enable("false")) multiplexer_1 (
    .in0(registerfile16_1_output2), .in1(controlunit_1_imm), .out(multiplexer_1_out),
    .sel(controlunit_1_imm_select));
  ALU alu_1 (.xyz(controlunit_1_alu_op), .a(registerfile16_1_output1), .b(multiplexer_1_out), .out(alu_1_out));
  Multiplexer #(.width(18), .enable("false")) multiplexer_2 (
    .in0(alu_1_out), .in1(ram_1_data), .out(multiplexer_2_out), .sel(controlunit_1_winput));
  RegisterFile16 registerfile16_1 (
    .rd1(controlunit_1_rd1), .rd2(controlunit_1_rd2), .\input (multiplexer_2_out), .wd1(controlunit_1_wd),
    .we(controlunit_1_we), .output1(registerfile16_1_output1), .output2(registerfile16_1_output2));

  // Notes on the sheet:
  //   ROM
  //   contents of rom_1 (hex, n*v repeats v):
  //   4000 4011 4022 4033 4044 20000 20011 17f22 10133 18211 14111 3c304 14144 10100 3fffd 28024 28030
  //   3f000
  //   RAM
endmodule

// SE4
module SignExtend4 (
  input  [3:0] \input ,
  output [17:0] \output 
);


  assign \output  = {{15{\input [3]}}, \input [2:0]};
endmodule

// SE6
module SignExtend6 (
  input  [5:0] \input ,
  output [17:0] \output 
);


  assign \output  = {{13{\input [5]}}, \input [4:0]};
endmodule

// SE12
module SignExtend12 (
  input  [11:0] \input ,
  output [17:0] \output 
);


  assign \output  = {{7{\input [11]}}, \input [10:0]};
endmodule

module PC (
  input  [17:0] branch_offset,
  input  we,
  input  branch,
  input  [17:0] op1,
  input  [17:0] op2,
  input  [2:0] nzp,
  output [17:0] \output 
);

  wire and_1_out, and_2_out, and_3_out, and_4_out, comparator18_1_out_eq, comparator18_1_out_gt,
       comparator18_1_out_lt, or_1_out;
  wire [17:0] add18_1_output, multiplexer_1_out;

  Comparator18 comparator18_1 (
    .a(op1), .b(op2), .out_lt(comparator18_1_out_lt), .out_eq(comparator18_1_out_eq),
    .out_gt(comparator18_1_out_gt));
  Register #(.width(18)) PC (.D(add18_1_output), .Q(\output ), .clk(we));  // open: en, clr
  and and_1 (and_1_out, comparator18_1_out_lt, nzp[2]);
  and and_2 (and_2_out, comparator18_1_out_eq, nzp[1]);
  and and_3 (and_3_out, comparator18_1_out_gt, nzp[0]);
  Multiplexer #(.width(18), .disabled(0), .enable("false")) multiplexer_1 (
    .in0(18'h1), .in1(branch_offset), .out(multiplexer_1_out), .sel(and_4_out));
  and and_4 (and_4_out, branch, or_1_out);
  or or_1 (or_1_out, and_1_out, and_2_out, and_3_out);
  ADD18 add18_1 (.input0(\output ), .input1(multiplexer_1_out), .\output (add18_1_output));  // open: carry_out
endmodule

// Control\nUnit
module ControlUnit (
  input  [17:0] inst,
  input  clock,
  output [9:0] ram_address,
  output [2:0] alu_op,
  output s_ram,
  output imm_select,
  output [17:0] imm,
  output winput,
  output [3:0] rd1,
  output [3:0] rd2,
  output [3:0] wd,
  output we,
  output [2:0] nzp,
  output branch,
  output pcwe,
  output [17:0] branch_offset
);

  wire and_1_out, and_3_out, and_5_out;
  wire [1:0] multiplexer_3_out, or_1_out, State_Register_q;
  wire [17:0] signextend4_1_output, signextend12_1_output;

  and and_1 (and_1_out, inst[14], inst[13], inst[12]);
  Multiplexer #(.width(18), .enable("false")) multiplexer_1 (
    .in0(signextend4_1_output), .in1(signextend12_1_output), .out(branch_offset), .sel(and_1_out));
  and and_2 (branch, inst[17], inst[16], inst[15]);
  SignExtend4 signextend4_1 (.\input (inst[3:0]), .\output (signextend4_1_output));
  SignExtend12 signextend12_1 (.\input (inst[11:0]), .\output (signextend12_1_output));
  and and_3 (and_3_out, inst[15], inst[17]);  // AND_Gate
  SignExtend6 signextend6_1 (.\input (inst[13:8]), .\output (imm));
  Decoder #(.select(2), .enable("false")) decoder_1 (
    .out1(s_ram), .out2(we), .out3(pcwe), .sel(State_Register_q));  // open: out0
  Register #(.width(2)) State_Register (.D(multiplexer_3_out), .Q(State_Register_q), .clk(clock));  // open: en, clr
  and and_4 (winput, ~inst[15], ~inst[16], inst[17]);  // AND_Gate
  and and_5 (and_5_out, inst[15], ~inst[16], inst[17]);  // AND_Gate
  or or_1 (or_1_out[0], branch, and_3_out);
  or or_2 (or_1_out[1], branch, ~and_3_out);  // OR_Gate
  Multiplexer #(.width(4), .disabled(0), .enable("false")) multiplexer_2 (
    .in0(inst[7:4]), .in1(inst[3:0]), .out(rd1), .sel(and_5_out));
  Multiplexer #(.select(2), .width(2), .disabled(0), .enable("false")) multiplexer_3 (
    .in0(or_1_out), .in1(2'b11), .in2(2'b11), .in3(2'b00), .out(multiplexer_3_out), .sel(State_Register_q));

  assign alu_op = inst[17:15];
  assign imm_select = inst[14];
  assign nzp = inst[14:12];
  assign ram_address = inst[13:4];
  assign rd2 = inst[11:8];
  assign wd = inst[3:0];
endmodule

module ALU (
  input  [2:0] xyz,
  input  [17:0] a,
  input  [17:0] b,
  output [17:0] out
);

  wire decoder_1_out0, decoder_1_out1, decoder_1_out2, decoder_1_out3;
  wire [17:0] add18_1_output, and_1_out, or_1_out, xor_1_out;

  assign and_1_out = a & b;  // AND_Gate and_1, 18 bits wide
  assign or_1_out = a | b;  // OR_Gate or_1, 18 bits wide
  ADD18 add18_1 (.input0(a), .input1(b), .\output (add18_1_output));  // open: carry_out
  assign xor_1_out = a ^ b;  // XOR_Gate xor_1, 18 bits wide
  Decoder #(.select(2), .disabled(0), .enable("false")) decoder_1 (
    .out0(decoder_1_out0), .out1(decoder_1_out1), .out2(decoder_1_out2), .out3(decoder_1_out3), .sel(xyz[1:0]));
  assign out = decoder_1_out0 ? and_1_out : 18'bz;  // Controlled_Buffer controlled_buffer_1
  assign out = decoder_1_out1 ? or_1_out : 18'bz;  // Controlled_Buffer controlled_buffer_2
  assign out = decoder_1_out2 ? add18_1_output : 18'bz;  // Controlled_Buffer controlled_buffer_3
  assign out = decoder_1_out3 ? xor_1_out : 18'bz;  // Controlled_Buffer controlled_buffer_4
endmodule
